// Digital circuit astro_genius.dig as structural Verilog
module astro_genius (
  input  _1_Hz,
  input  _10000_Hz,
  input  _1000_Hz,
  input  especial,
  input  easy,
  input  \medium ,
  input  hard,
  output Pronto,
  output [4:0] Jogo_principal,
  output [4:0] Coordena,
  output [4:0] Compara_tiros_e_asteroides,
  output [4:0] Move_tiros,
  output [4:0] Compara_asteroides__nave_e_tiros,
  output [4:0] Move_asteroides,
  output [3:0] Registra_tiros,
  output [3:0] Vidas,
  output Conta_Contador,
  output rco,
  output reset,
  output [15:0] cont,
  output [9:0] pontos
);

  wire button_1_out, Iniciar_out, Reset_out, switch_1_b, u_astro_genius_db_aste_renderizado,
       u_astro_genius_db_tiro_renderizado;
  wire [3:0] register_1_q, register_2_q, register_3_q, register_4_q, u_astro_genius_db_asteroide_x,
       u_astro_genius_db_asteroide_y, u_astro_genius_db_estado_uc_gera_frame,
       u_astro_genius_db_estado_uc_renderiza, u_astro_genius_db_tiro_x, u_astro_genius_db_tiro_y,
       u_astro_genius_db_uc_gera_asteroide, u_astro_genius_matriz_y;
  wire [5:0] UP_out;
  wire [14:0] u_astro_genius_matriz_x;

  Button UP (.out(UP_out[5]));
  Button DOWN (.out(UP_out[4]));
  Switch switch_1 (.A(_1000_Hz), .B(switch_1_b));
  Switch switch_2 (.A(_1_Hz), .B(switch_1_b));
  Switch switch_3 (.A(_10000_Hz), .B(switch_1_b));
  Button button_1 (.out(button_1_out));
  Switch switch_4 (.A(button_1_out), .B(switch_1_b));
  Button u_Reset (.out(Reset_out));
  Button Iniciar (.out(Iniciar_out));
  Button LEFT (.out(UP_out[3]));
  Button RIGHT (.out(UP_out[2]));
  astro_genius #(.applicationType("IVERILOG")) u_astro_genius (
    .clock(switch_1_b), .reset(Reset_out), .iniciar(Iniciar_out), .dificuldade({easy, \medium , hard}),
    .chaves({UP_out[5:2], especial, UP_out[0]}), .pronto(Pronto), .db_estado_jogo_principal(Jogo_principal),
    .db_estado_coordena_asteroides_tiros(Coordena),
    .db_estado_compara_tiros_e_asteroide(Compara_tiros_e_asteroides), .db_estado_move_tiros(Move_tiros),
    .db_estado_compara_asteroides_com_nave_e_tiros(Compara_asteroides__nave_e_tiros),
    .db_estado_move_asteroides(Move_asteroides), .db_estado_registra_tiro(Registra_tiros), .db_vidas(Vidas),
    .db_asteroide_x(u_astro_genius_db_asteroide_x), .db_asteroide_y(u_astro_genius_db_asteroide_y),
    .db_tiro_x(u_astro_genius_db_tiro_x), .db_tiro_y(u_astro_genius_db_tiro_y),
    .db_aste_renderizado(u_astro_genius_db_aste_renderizado),
    .db_tiro_renderizado(u_astro_genius_db_tiro_renderizado),
    .db_estado_uc_gera_frame(u_astro_genius_db_estado_uc_gera_frame), .matriz_x(u_astro_genius_matriz_x),
    .matriz_y(u_astro_genius_matriz_y), .db_estado_uc_renderiza(u_astro_genius_db_estado_uc_renderiza),
    .db_uc_gera_asteroide(u_astro_genius_db_uc_gera_asteroide),
    .db_conta_contador_gera_asteroide(Conta_Contador), .db_rco_contador_gera_aste(rco),
    .db_reset_contador_gera_asteroide(reset), .db_contador_163(cont), .db_pontos(pontos));
  Button SHIFT (.out(UP_out[0]));
  Seven_Seg_Hex seven_seg_hex_1 (.d(u_astro_genius_db_uc_gera_asteroide), .dp(1'b0));
  LedMatrix #(.colAddrBits(4), .rowDataBits(15)) ledmatrix_1 (
    .rows(u_astro_genius_matriz_x), .column(u_astro_genius_matriz_y));
  Seven_Seg_Hex seven_seg_hex_2 (.d(u_astro_genius_db_estado_uc_renderiza), .dp(1'b0));
  Seven_Seg_Hex seven_seg_hex_3 (.d(u_astro_genius_db_estado_uc_gera_frame), .dp(1'b0));
  Register #(.Bits(4)) register_1 (
    .D(u_astro_genius_db_asteroide_x), .C(switch_1_b), .en(u_astro_genius_db_aste_renderizado),
    .Q(register_1_q));
  Register #(.Bits(4)) register_2 (
    .D(u_astro_genius_db_asteroide_y), .C(switch_1_b), .en(u_astro_genius_db_aste_renderizado),
    .Q(register_2_q));
  Register #(.Bits(4)) register_3 (
    .D(u_astro_genius_db_tiro_x), .C(switch_1_b), .en(u_astro_genius_db_tiro_renderizado), .Q(register_3_q));
  Register #(.Bits(4)) register_4 (
    .D(u_astro_genius_db_tiro_y), .C(switch_1_b), .en(u_astro_genius_db_tiro_renderizado), .Q(register_4_q));
  Seven_Seg_Hex seven_seg_hex_4 (.d(register_1_q), .dp(1'b0));
  Seven_Seg_Hex seven_seg_hex_5 (.d(register_2_q), .dp(1'b0));
  Seven_Seg_Hex seven_seg_hex_6 (.d(register_3_q), .dp(1'b0));
  Seven_Seg_Hex seven_seg_hex_7 (.d(register_4_q), .dp(1'b0));

  // Notes on the sheet:
  //   _10000_Hz: Hz: 10000
  //   _1000_Hz: Hz: 1000
  //   asteroide
  //   tiros
endmodule

/* Code of astro_genius:
module astro_genius (
        input clock,
        input reset,
        input iniciar,
        input [2:0] dificuldade,
        input [5:0] chaves,
        output pronto,

        /* sinais de depuracao * /
        output [4:0] db_estado_jogo_principal,
        output [4:0] db_estado_coordena_asteroides_tiros,
        output [4:0] db_estado_compara_tiros_e_asteroide,
        output [4:0] db_estado_move_tiros,
        output [4:0] db_estado_compara_asteroides_com_nave_e_tiros,
        output [4:0] db_estado_move_asteroides,
        output [3:0] db_estado_registra_tiro,
        output [3:0] db_vidas,
        output [3:0] db_asteroide_x,
        output [3:0] db_asteroide_y,
        output [3:0] db_tiro_x,
        output [3:0] db_tiro_y,
        output db_aste_renderizado,
        output db_tiro_renderizado,
        output [3:0] db_estado_uc_gera_frame,
        output [14:0] matriz_x,
        output [3:0] matriz_y,
        output [3:0] db_estado_uc_renderiza,
        output [3:0] db_uc_gera_asteroide,
        output db_conta_contador_gera_asteroide,
        output db_rco_contador_gera_aste,
        output db_reset_contador_gera_asteroide,
        output [15:0] db_contador_163,
        output [9:0] db_pontos
);

//wires da conexão da UC principal com outros modulos
wire wire_vidas;
wire wire_fim_movimentacao_asteroides_e_tiros;
wire wire_inicia_registra_tiros;
wire wire_inicia_movimentacao_asteroides_e_tiros;
wire wire_reset_maquinas;
wire wire_reset_contador_asteroides_uc_principal;
wire wire_reset_contador_tiro_uc_principal; //sintaxe: o final indica de onde está saindo o fio
wire wire_enable_decrementador; 
wire wire_reset_contador_vidas;

wire wire_ocorreu_tiro;
wire wire_ocorreu_jogada;
wire wire_reset_reg_jogada;
wire wire_enable_reg_jogada;

wire wire_destruido_aste;

wire [3:0] wire_aste_coor_x;
wire [3:0] wire_aste_coor_y;
wire [1:0] wire_opcode_mux_out;
wire wire_reset_pontuacao_uc_principal;

assign db_aste_renderizado = wire_aste_renderizado;
assign db_tiro_renderizado = wire_tiro_renderizado;
assign db_asteroide_x = wire_aste_renderizado ? wire_aste_coor_x : 4'b0000;
assign db_asteroide_y = wire_aste_renderizado ? wire_aste_coor_y : 4'b0000;

assign db_tiro_x = wire_tiro_renderizado ? wire_tiro_coor_x : 4'b0000;
assign db_tiro_y = wire_tiro_renderizado ? wire_tiro_coor_y : 4'b0000;

wire wire_termina_uc_jogo_principal;

uc_jogo_principal uc_jogo_principal(
    /* inputs * /
    .clock(clock),
    .iniciar(iniciar),
    .reset(reset),
    .vidas(~wire_vidas), //rco do decrementador
    .fim_movimentacao_asteroides_e_tiros(wire_fim_movimentacao_asteroides_e_tiros), 
    .fim_registra_tiros(wire_tiro_registrado),
    .ocorreu_tiro(wire_ocorreu_tiro), 
    .ocorreu_jogada(wire_ocorreu_jogada), //saida do edge detector
    /* outputs * /
    .enable_reg_jogada(wire_enable_reg_jogada),
    .reset_reg_jogada(wire_reset_reg_jogada),
    .reset_pontuacao(wire_reset_pontuacao_uc_principal),
    .inicia_registra_tiros(wire_inicia_registra_tiros),
    .inicia_movimentacao_asteroides_e_tiros(wire_inicia_movimentacao_asteroides_e_tiros), 
    .reset_contador_asteroides(wire_reset_contador_asteroides_uc_principal),
    .reset_contador_tiro(wire_reset_contador_tiro_uc_principal),
    .reset_contador_vidas(wire_reset_contador_vidas),
    .reset_maquinas(wire_reset_maquinas),
    .pronto(pronto),
    .termina(wire_termina_uc_jogo_principal),
    .db_estado_jogo_principal(db_estado_jogo_principal)
);
// wires genericos 
wire wire_rco_contador_tiro;
wire wire_rco_contador_asteroides;




// wires da conexão da uc_coordena_asteroides_tiros com outros modulos
// INPUT
wire wire_fim_move_tiros;
wire wire_fim_move_asteroides;
wire wire_fim_comparacao_asteroides_com_a_nave_e_tiros;
wire wire_fim_comparacao_tiros_e_asteroides;

// OUTPUT
wire wire_movimenta_tiro;
wire wire_sinal_movimenta_asteroides;
wire wire_sinal_compara_tiros_e_asteroides_uc_coordena_asteroides_tiros;
wire wire_sinal_compara_asteroides_com_a_nave_e_tiro;
wire wire_sinal_compara_tiros_e_asteroide_uc_compara_asteroides_com_nave_e_tiros;
wire wire_inicia_gera_frame_uc_coordena_asteroides_tiros;
wire wire_fim_gera_frame_uc_gera_frame;
wire wire_pausar_renderizacao;
wire wire_gera_asteroide;
wire wire_rco_contador_gera_aste;
wire reset_contador_gera_aste;
wire [15:0] wire_out_contador_163;

wire wire_rco_contador_movimenta_tiro;
wire wire_rco_contador_movimenta_asteroide;
wire wire_reset_contador_movimenta_tiro;
wire wire_reset_contador_movimenta_asteroide;
assign db_contador_163 = wire_out_contador_163;
assign db_conta_contador_gera_asteroide = wire_conta_contador_gera_asteroide;
assign db_rco_contador_gera_aste = wire_rco_contador_gera_aste;
assign db_reset_contador_gera_asteroide = wire_reset_contador_gera_asteroide;

parameter tiro_easy = 16'd1500;
parameter tiro_medium = 16'd1000;
parameter tiro_hard = 16'd500;

parameter tempo_move_asteroide_easy = 16'd6000;
parameter tempo_move_asteroide_medium = 16'd3000;
parameter tempo_move_asteroide_hard = 16'd1000;

parameter tempo_gera_asteroide_easy = 16'd6000;
parameter tempo_gera_asteroide_medium = 16'd3000;
parameter tempo_gera_asteroide_hard = 16'd1000;



wire [15:0] tempo_gera_aste;
wire [15:0] tempo_move_aste;
wire [15:0] tempo_move_tiro;

assign tempo_gera_aste = (dificuldade == 3'b100) ? tempo_gera_asteroide_easy :
                              (dificuldade == 3'b010) ? tempo_gera_asteroide_medium : tempo_gera_asteroide_hard;
                          
assign tempo_move_aste = (dificuldade == 3'b100) ? tempo_move_asteroide_easy:
                              (dificuldade == 3'b010) ? tempo_move_asteroide_medium : tempo_move_asteroide_hard;


assign tempo_move_tiro = (dificuldade == 3'b100) ? tiro_easy :
                              (dificuldade == 3'b010) ? tiro_medium : tiro_hard;

contador_163 #(16) contador_gera_asteroide  ( 
    /* inputs * /
    .clock(clock), 
    .clr(wire_reset_contador_gera_asteroide), 
    .ld(1'b0), 
    .ent(1'b1), 
    .enp(wire_conta_contador_gera_asteroide), 
    .D(),
    .Max(tempo_gera_aste),
    /* outputs * /
    .Q(wire_out_contador_163),
    .rco(wire_rco_contador_gera_aste)
);

contador_163 #(16) contador_movimenta_tiro  ( 
    /* inputs * /
    .clock(clock), 
    .clr(wire_reset_contador_movimenta_tiro), 
    .ld(1'b0), 
    .ent(1'b1), 
    .enp(1'b1), 
    .D(),
    .Max(tempo_move_tiro),
    /*outputs* /
    .Q(),
    .rco(wire_rco_contador_movimenta_tiro)
);

contador_163 #(16) contador_movimenta_asteroide  ( 
    /* inputs * /
    .clock(clock), 
    .clr(wire_reset_contador_movimenta_asteroide), 
    .ld(1'b0), 
    .ent(1'b1), 
    .enp(1'b1), 
    .D(),
    .Max(tempo_move_aste),
    /*outputs* /
    .Q(),
    .rco(wire_rco_contador_movimenta_asteroide)
);

uc_coordena_asteroides_tiros uc_coordena_asteroides_tiros(
    /* inputs * /
    .clock(clock),
    .reset(wire_reset_maquinas),
    .move_tiro_e_asteroides(wire_inicia_movimentacao_asteroides_e_tiros),
    .rco_contador_movimenta_tiros(wire_rco_contador_movimenta_tiro),
    .rco_contador_movimenta_asteroides(wire_rco_contador_movimenta_asteroide),
    .fim_move_tiros(wire_fim_move_tiros),
    .fim_move_asteroides(wire_fim_move_asteroides),
    .fim_comparacao_asteroides_com_a_nave_e_tiros(wire_fim_comparacao_asteroides_com_a_nave_e_tiros),
    .fim_comparacao_tiros_e_asteroides(wire_fim_comparacao_tiros_e_asteroides),
    .fim_gera_frame(wire_fim_gera_frame_uc_gera_frame),
    .fim_gera_asteroide(wire_fim_gera_asteroide),
    .gera_aste(wire_rco_contador_gera_aste),
    .termina_operacao(wire_termina_uc_jogo_principal),
    /* outputs * /
    .movimenta_tiro(wire_movimenta_tiro),
    .sinal_movimenta_asteroides(wire_sinal_movimenta_asteroides),
    .sinal_compara_tiros_e_asteroides(wire_sinal_compara_tiros_e_asteroides_uc_coordena_asteroides_tiros ),
    .sinal_compara_asteroides_com_a_nave_e_tiro(wire_sinal_compara_asteroides_com_a_nave_e_tiro),
    .fim_move_tiro_e_asteroides(wire_fim_movimentacao_asteroides_e_tiros),
    .db_estado_coordena_asteroides_tiros(db_estado_coordena_asteroides_tiros),
    .gera_frame(wire_inicia_gera_frame_uc_coordena_asteroides_tiros),
    .pausar_renderizacao(wire_pausar_renderizacao),
    .gera_asteroide(wire_gera_asteroide),
    .reset_gerador_random(wire_reset_gerador_random)
);

wire wire_reset_contador_asteroides_uc_gera_asteroide;
wire wire_conta_contador_asteroides_uc_gera_asteroide;
wire wire_enable_mem_aste_uc_gera_asteroide;
wire wire_enable_load_aste_uc_gera_asteroide;
wire wire_new_loaded_aste_uc_gera_asteroide;
wire wire_conta_contador_gera_asteroide;
wire wire_reset_contador_gera_asteroide;

uc_gera_asteroide uc_gera_asteroide (
    /* input * /
    .clock(clock)        ,
    .reset(wire_reset_maquinas),
    .gera_asteroide(wire_gera_asteroide),      
    .rco_contador_asteroide(wire_rco_contador_asteroides),
    .asteroide_renderizado(wire_aste_renderizado),

    /* output * /
    .reset_contador_asteroide(wire_reset_contador_asteroides_uc_gera_asteroide),
    .conta_contador_asteroide(wire_conta_contador_asteroides_uc_gera_asteroide),
    .conta_contador_gera_asteroide(wire_conta_contador_gera_asteroide),
    .reset_contador_gera_asteroide(wire_reset_contador_gera_asteroide),
    .enable_mem_aste(wire_enable_mem_aste_uc_gera_asteroide),
    .enable_load_aste(wire_enable_load_aste_uc_gera_asteroide),
    .new_loaded_aste(wire_new_loaded_aste_uc_gera_asteroide),
    .fim_gera_asteroide(wire_fim_gera_asteroide),
    .db_uc_gera_asteroide(db_uc_gera_asteroide)
);


wire wire_conta_contador_asteroides_uc_gera_frame;
wire wire_conta_contador_tiro_uc_gera_frame;
wire wire_reset_contador_tiro_uc_gera_frame;
wire wire_reset_contador_asteroide_uc_gera_frame;
wire wire_clear_mem_frame;
wire wire_enable_mem_frame;
wire [1:0] wire_select_mux_gera_frame;

uc_gera_frame uc_gera_frame (
        // entradas
        .clock(clock),
        .reset(reset_maquinas),
        .gera_frame(wire_inicia_gera_frame_uc_coordena_asteroides_tiros),
        .rco_contador_asteroides(wire_rco_contador_asteroides),
        .rco_contador_tiro(wire_rco_contador_tiro),
        .loaded_tiro(wire_tiro_renderizado),
        .loaded_asteroide(wire_aste_renderizado),

        //saidas
        .conta_contador_asteroide(wire_conta_contador_asteroides_uc_gera_frame),
        .conta_contador_tiro(wire_conta_contador_tiro_uc_gera_frame),
        .reset_contador_tiro(wire_reset_contador_tiro_uc_gera_frame),
        .reset_contador_asteroide(wire_reset_contador_asteroide_uc_gera_frame),
        .clear_mem_frame(wire_clear_mem_frame),
        .enable_mem_frame(wire_enable_mem_frame),
        .fim_gera_frame(wire_fim_gera_frame_uc_gera_frame),
        .select_mux_gera_frame(wire_select_mux_gera_frame),
        .db_estado_uc_gera_frame(db_estado_uc_gera_frame)
);


wire [3:0] wire_entrada_x_memoria_frame;
wire [3:0] wire_entrada_y_memoria_frame;

assign wire_entrada_x_memoria_frame = (wire_select_mux_gera_frame == 2'b00) ? wire_aste_coor_x : 
                                      (wire_select_mux_gera_frame == 2'b01) ? wire_tiro_coor_x : 
                                      (wire_select_mux_gera_frame == 2'b10) ? 4'b0111          : wire_saida_contador_frame ;
 
assign wire_entrada_y_memoria_frame = (wire_select_mux_gera_frame == 2'b00) ? wire_aste_coor_y : 
                                      (wire_select_mux_gera_frame == 2'b01) ? wire_tiro_coor_y :
                                      (wire_select_mux_gera_frame == 2'b10) ? 4'b0111          : wire_saida_contador_frame;

// assign wire_entrada_x_memoria_frame = wire_tiro_coor_x;
 
// assign wire_entrada_y_memoria_frame = wire_tiro_coor_y;

memoria_frame memoria_frame(
            // input
            .coor_x(wire_entrada_y_memoria_frame),
            .coor_y(wire_entrada_x_memoria_frame),
            .clk   (clock),
            .clear(wire_clear_mem_frame),
            .we   (wire_enable_mem_frame),
            // output
            .saida_x(matriz_x),
            .saida_y(matriz_y)
            );

wire wire_rco_contador_frame;
wire wire_conta_contador_frame;
wire wire_reset_contador_frame;

uc_renderiza uc_renderiza (
        .clock(clock)                    ,
        .reset(wire_reset_maquinas)                    ,
        .pausar_renderizacao(wire_pausar_renderizacao)      ,
        .rco_contador_frame(wire_rco_contador_frame)    ,

        .reset_contador_frame(wire_reset_contador_frame) ,    
        .conta_contador_frame(wire_conta_contador_frame) ,    
        .db_estado_uc_renderiza(db_estado_uc_renderiza)
);





 contador_m #(15, 4) contador_renderiza(
   .clock(clock),
   .zera_as(wire_reset_contador_frame),
   .zera_s(1'b0),
   .conta(wire_conta_contador_frame),
   .Q(wire_saida_contador_frame),
   .fim(wire_rco_contador_frame),
   .meio()
  );
wire [3:0] wire_saida_contador_frame; 

wire [3:0] entrada_y_mem_frame;



// wires da conexão da uc_compara_tiros_e_asteroides com outros modulos
// INPUT
wire wire_posicao_tiro_igual_asteroide;

// principal
wire wire_tiro_renderizado;
wire wire_aste_renderizado;

// OUTPUT
wire wire_reset_contador_asteroides_uc_compara_tiros_e_asteroides;
wire wire_reset_contador_tiros_uc_compara_tiros_e_asteroides;
wire wire_enable_load_tiro_uc_compara_tiros_e_asteroides;
wire wire_enable_load_asteroide_uc_compara_tiros_e_asteroides;
wire wire_new_loaded_tiro_uc_compara_tiros_e_asteroides;
wire wire_new_loaded_asteroide_uc_compara_tiros_e_asteroides;
wire wire_new_destruido_asteroide_uc_compara_tiros_e_asteroides;
wire wire_incrementa_pontos_uc_compara_tiros_e_asteroides;


wire wire_conta_contador_asteroides_uc_compara_tiros_e_asteroides;
wire wire_conta_contador_tiros_uc_compara_tiros_e_asteroides;


uc_compara_tiros_e_asteroides uc_compara_tiros_e_asteroides (
    /* inputs * /
    .clock(clock),
    .reset(wire_reset_maquinas),
    .compara_tiros_e_asteroides(wire_sinal_compara_tiros_e_asteroides_uc_coordena_asteroides_tiros |
                                wire_sinal_compara_tiros_e_asteroide_uc_compara_asteroides_com_nave_e_tiros
                                ),
    .posicao_tiro_igual_asteroide(wire_posicao_tiro_igual_asteroide),
    .rco_contador_asteroides(wire_rco_contador_asteroides),
    .rco_contador_tiros(wire_rco_contador_tiro),
    .tiro_renderizado(wire_tiro_renderizado),
    .aste_renderizado(wire_aste_renderizado),
    /* outputs * /
    .reset_contador_asteroides(wire_reset_contador_asteroides_uc_compara_tiros_e_asteroides),
    .reset_contador_tiros(wire_reset_contador_tiros_uc_compara_tiros_e_asteroides),
    .enable_load_tiro(wire_enable_load_tiro_uc_compara_tiros_e_asteroides),
    .enable_load_asteroide(wire_enable_load_asteroide_uc_compara_tiros_e_asteroides),
    .loaded_tiro(wire_new_loaded_tiro_uc_compara_tiros_e_asteroides),
    .loaded_asteroide(wire_new_loaded_asteroide_uc_compara_tiros_e_asteroides),
    .asteroide_destruido(wire_new_destruido_asteroide_uc_compara_tiros_e_asteroides),
    .conta_contador_asteroides(wire_conta_contador_asteroides_uc_compara_tiros_e_asteroides),
    .conta_contador_tiros(wire_conta_contador_tiros_uc_compara_tiros_e_asteroides),
    .incrementa_pontos(wire_incrementa_pontos_uc_compara_tiros_e_asteroides),
    .s_fim_comparacao(wire_fim_comparacao_tiros_e_asteroides),
    .db_estado_compara_tiros_e_asteroide(db_estado_compara_tiros_e_asteroide)
);



// wires da conexão da uc_move_tiros com outros modulos
// INPUT
wire [1:0] wire_opcode_tiro;
wire wire_x_borda_max_tiro;
wire wire_y_borda_max_tiro;
wire wire_x_borda_min_tiro;
wire wire_y_borda_min_tiro;

// OUTPUT
wire [1:0] wire_select_mux_pos_tiro_uc_move_tiros;
wire wire_select_mux_coor_tiro_uc_move_tiros;
wire wire_select_soma_sub_uc_move_tiros;
wire wire_reset_contador_tiro_uc_move_tiros;
wire wire_conta_contador_tiro_uc_move_tiros;
wire wire_enable_mem_tiro_uc_move_tiros;
wire wire_enable_load_tiro_uc_move_tiros;
wire wire_new_loaded_tiro_uc_move_tiros;

uc_move_tiros uc_move_tiros (
    /* inputs * /
    .clock(clock),
    .movimenta_tiro(wire_movimenta_tiro),
    .reset(wire_reset_maquinas),
    .opcode_tiro(wire_opcode_tiro),
    .loaded_tiro(wire_tiro_renderizado),
    .rco_contador_tiro(wire_rco_contador_tiro),
    .x_borda_max_tiro(wire_x_borda_max_tiro),
    .y_borda_max_tiro(wire_y_borda_max_tiro),
    .x_borda_min_tiro(wire_x_borda_min_tiro),
    .y_borda_min_tiro(wire_y_borda_min_tiro), 
    /* outputs * /
    .select_mux_pos_tiro (wire_select_mux_pos_tiro_uc_move_tiros),   
    .select_mux_coor_tiro(wire_select_mux_coor_tiro_uc_move_tiros),   
    .select_soma_sub(wire_select_soma_sub_uc_move_tiros),  
    .reset_contador_tiro(wire_reset_contador_tiro_uc_move_tiros),
    .conta_contador_tiro(wire_conta_contador_tiro_uc_move_tiros), 
    .reset_contador_movimenta_tiro(wire_reset_contador_movimenta_tiro),
    .enable_mem_tiro(wire_enable_mem_tiro_uc_move_tiros), 
    .enable_load_tiro(wire_enable_load_tiro_uc_move_tiros),
    .new_loaded(wire_new_loaded_tiro_uc_move_tiros),                
    .movimentacao_concluida_tiro(wire_fim_move_tiros), 
    .db_estado_move_tiros(db_estado_move_tiros)
);

// INPUT
wire wire_posicao_asteroide_igual_nave;

// OUTPUT
wire wire_new_loaded_asteroide_uc_compara_asteroides_com_nave_e_tiros;
wire wire_new_destruido_asteroide_uc_compara_asteroides_com_nave_e_tiros;
wire wire_enable_load_asteroides_uc_compara_asteroides_com_nave_e_tiros;
wire wire_reset_contador_asteroides_uc_compara_asteroides_com_nave_e_tiros;

wire wire_conta_contador_asteroides_uc_compara_asteroides_com_nave_e_tiros;


uc_compara_asteroides_com_nave_e_tiros uc_compara_asteroides_com_nave_e_tiros (
    /* inputs * /
    .clock(clock),
    .reset(wire_reset_maquinas),
    .iniciar_comparacao_tiros_nave_asteroides(wire_sinal_compara_asteroides_com_a_nave_e_tiro),
    .posicao_asteroide_igual_nave(wire_posicao_asteroide_igual_nave),
    .ha_vidas(~wire_vidas),
    .rco_contador_asteroides(wire_rco_contador_asteroides),
    .fim_compara_tiros_e_asteroides(wire_fim_comparacao_tiros_e_asteroides),
    .loaded_asteroide(wire_aste_renderizado),
    .destruido_asteroide(wire_destruido_aste),
    /* outputs * /
    .enable_decrementador(wire_enable_decrementador),
    .new_loaded_asteroide(wire_new_loaded_asteroide_uc_compara_asteroides_com_nave_e_tiros),
    .new_destruido_asteroide(wire_new_destruido_asteroide_uc_compara_asteroides_com_nave_e_tiros),
    .fim_compara_asteroides_com_tiros_e_nave(wire_fim_comparacao_asteroides_com_a_nave_e_tiros),
    .enable_load_asteroide(wire_enable_load_asteroides_uc_compara_asteroides_com_nave_e_tiros),
    .conta_contador_asteroides(wire_conta_contador_asteroides_uc_compara_asteroides_com_nave_e_tiros), 
    .sinal_compara_tiros_e_asteroide(wire_sinal_compara_tiros_e_asteroide_uc_compara_asteroides_com_nave_e_tiros),
    .reset_contador_asteroides(wire_reset_contador_asteroides_uc_compara_asteroides_com_nave_e_tiros),
    .db_estado_compara_asteroides_com_nave_e_tiros(db_estado_compara_asteroides_com_nave_e_tiros)
);

// INPUT

wire [1:0] wire_opcode_aste;

// OUTPUT
wire [1:0] wire_select_mux_pos_aste_uc_move_asteroides;
wire wire_select_mux_coor_aste_uc_move_asteroides;
wire wire_select_soma_sub_uc_move_asteroides;
wire wire_reset_contador_aste_uc_move_asteroides;
wire wire_conta_contador_aste_uc_move_asteroides;
wire wire_enable_mem_aste_uc_move_asteroides;

uc_move_asteroides uc_move_asteroides(
    /* inputs * /
    .clock(clock),
    .movimenta_aste(wire_sinal_movimenta_asteroides),
    .reset(wire_reset_maquinas),
    .opcode_aste(wire_opcode_aste),
    .loaded_aste(wire_aste_renderizado),
    .rco_contador_aste(wire_rco_contador_asteroides),
     /* outputs * /    
    .select_mux_pos_aste(wire_select_mux_pos_aste_uc_move_asteroides),   
    .select_mux_coor_aste(wire_select_mux_coor_aste_uc_move_asteroides),  
    .select_soma_sub(wire_select_soma_sub_uc_move_asteroides),  
    .reset_contador_aste(wire_reset_contador_aste_uc_move_asteroides),
    .conta_contador_aste(wire_conta_contador_aste_uc_move_asteroides), 
    .reset_contador_movimenta_asteroide(wire_reset_contador_movimenta_asteroide),
    .enable_mem_aste(wire_enable_mem_aste_uc_move_asteroides), 
    .movimentacao_concluida_aste(wire_fim_move_asteroides), 
    .db_estado_move_aste(db_estado_move_asteroides)

);

//Outputs
wire wire_enable_mem_tiro_uc_registra_tiro;
wire wire_enable_load_tiro_uc_registra_tiro;
wire wire_new_loaded_tiro_uc_registra_tiro;
wire wire_reset_contador_tiro_uc_registra_tiro;
wire wire_conta_contador_tiro_uc_registra_tiro;
wire [1:0] wire_select_mux_pos_tiro_uc_registra_tiro;

wire wire_tiro_registrado;

uc_registra_tiro uc_registra_tiro(
    /* inputs * /
    .clock(clock),
    .registra_tiro(wire_inicia_registra_tiros),
    .reset(wire_reset_maquinas),
    .loaded_tiro(wire_tiro_renderizado),
    .rco_contador_tiro(wire_rco_contador_tiro),
    /* outputs * /
    .enable_mem_tiro(wire_enable_mem_tiro_uc_registra_tiro), 
    .enable_load_tiro(wire_enable_load_tiro_uc_registra_tiro), 
    .new_load(wire_new_loaded_tiro_uc_registra_tiro),
    .clear_contador_tiro(wire_reset_contador_tiro_uc_registra_tiro), 
    .conta_contador_tiro(wire_conta_contador_tiro_uc_registra_tiro), 
    .select_mux_pos(wire_select_mux_pos_tiro_uc_registra_tiro), 
    .tiro_registrado(wire_tiro_registrado), 
    .db_estado_registra_tiro(db_estado_registra_tiro)

);


wire wire_reset_gerador_random;
wire wire_fim_gera_asteroide;

asteroide asteroide(
    /* inputs * /
    .clock(clock),
    .conta_contador_aste(wire_conta_contador_asteroides_uc_compara_tiros_e_asteroides|
                         wire_conta_contador_asteroides_uc_compara_asteroides_com_nave_e_tiros |
                         wire_conta_contador_aste_uc_move_asteroides | 
                         wire_conta_contador_asteroides_uc_gera_frame |
                         wire_conta_contador_asteroides_uc_gera_asteroide ),
    .reset_contador_aste(wire_reset_contador_asteroides_uc_principal | 
                         wire_reset_contador_asteroides_uc_compara_tiros_e_asteroides |
                         wire_reset_contador_asteroides_uc_compara_asteroides_com_nave_e_tiros |
                         wire_reset_contador_aste_uc_move_asteroides |
                         wire_reset_contador_asteroide_uc_gera_frame |
                         wire_reset_contador_asteroides_uc_gera_asteroide ),
    .select_mux_pos_aste(wire_select_mux_pos_aste_uc_move_asteroides),
    .select_mux_coor_aste(wire_select_mux_coor_aste_uc_move_asteroides),
    .select_soma_sub_aste(wire_select_soma_sub_uc_move_asteroides),
    .enable_reg_nave(),
    .reset_reg_nave(),
    .enable_mem_aste(wire_enable_mem_aste_uc_move_asteroides | wire_enable_mem_aste_uc_gera_asteroide),
    .enable_load_aste(wire_enable_load_asteroide_uc_compara_tiros_e_asteroides |
                      wire_enable_load_asteroides_uc_compara_asteroides_com_nave_e_tiros |
                      wire_enable_load_aste_uc_gera_asteroide),
    // .new_load_aste(wire_new_loaded_asteroide_uc_compara_tiros_e_asteroides | 
    //                wire_new_loaded_asteroide_uc_compara_asteroides_com_nave_e_tiros),
    .new_load_aste(wire_new_loaded_aste_uc_gera_asteroide),
    .new_destruido_aste(wire_new_destruido_asteroide_uc_compara_tiros_e_asteroides |
                        wire_new_destruido_asteroide_uc_compara_asteroides_com_nave_e_tiros),
    .reset_gerador_random(wire_reset_gerador_random),
    /* outputs * /
    .colisao_aste_com_nave(wire_posicao_asteroide_igual_nave),
    .rco_contador_aste(wire_rco_contador_asteroides),
    .opcode_aste(wire_opcode_aste),
    .destruido_aste(wire_destruido_aste),
    .loaded_aste(wire_aste_renderizado),
    .aste_coor_x(wire_aste_coor_x),
    .aste_coor_y(wire_aste_coor_y),
    .db_contador_aste(),
    .db_wire_saida_som_sub_aste()
);

wire [3:0] wire_tiro_coor_x;
wire [3:0] wire_tiro_coor_y;


tiro tiro (
    /* inputs * /
    .clock(clock),
    .conta_contador_tiro(wire_conta_contador_tiros_uc_compara_tiros_e_asteroides |
                         wire_conta_contador_tiro_uc_move_tiros |
                         wire_conta_contador_tiro_uc_registra_tiro |
                         wire_conta_contador_tiro_uc_gera_frame),
    .reset_contador_tiro(wire_reset_contador_tiro_uc_principal |
                         wire_reset_contador_tiros_uc_compara_tiros_e_asteroides |
                         wire_reset_contador_tiro_uc_move_tiros |
                         wire_reset_contador_tiro_uc_registra_tiro |
                         wire_reset_contador_tiro_uc_gera_frame),
    .select_mux_pos_tiro(wire_select_mux_pos_tiro_uc_move_tiros |
                         wire_select_mux_pos_tiro_uc_registra_tiro),
                         
    .select_mux_coor_tiro(wire_select_mux_coor_tiro_uc_move_tiros),
    .select_soma_sub_tiro(wire_select_soma_sub_uc_move_tiros),
    .enable_reg_nave(),
    .reset_reg_nave(),
    .enable_mem_tiro(wire_enable_mem_tiro_uc_move_tiros |
                    wire_enable_mem_tiro_uc_registra_tiro),
    .enable_load_tiro(wire_enable_load_tiro_uc_compara_tiros_e_asteroides |
                      wire_enable_load_tiro_uc_move_tiros |
                      wire_enable_load_tiro_uc_registra_tiro),
    .aste_coor_x(wire_aste_coor_x),
    .aste_coor_y(wire_aste_coor_y),
    // .new_load_tiro(wire_new_loaded_tiro_uc_compara_tiros_e_asteroides |
    //                wire_new_loaded_tiro_uc_move_tiros |
    //                wire_new_loaded_tiro_uc_registra_tiro),
    .new_load_tiro(wire_new_loaded_tiro_uc_registra_tiro),
    .opcode_registra_tiro(wire_opcode_mux_out),
    /* outputs * /
    .x_borda_min_tiro(wire_x_borda_min_tiro),
    .y_borda_min_tiro(wire_y_borda_min_tiro),
    .x_borda_max_tiro(wire_x_borda_max_tiro),
    .y_borda_max_tiro(wire_y_borda_max_tiro),
    .colisao_tiro_asteroide(wire_posicao_tiro_igual_asteroide),
    .rco_contador_tiro(wire_rco_contador_tiro),
    .opcode_tiro(wire_opcode_tiro),
    .loaded_tiro(wire_tiro_renderizado),
    .db_contador_tiro(),
    .db_wire_saida_som_sub_tiro(),
    .db_tiro_pos_x(wire_tiro_coor_x),
    .db_tiro_pos_y(wire_tiro_coor_y)
);

wire [3:0] wire_quantidade_vidas;
assign db_vidas = wire_quantidade_vidas;
decrementador #(4) decrementador( 
    /* inputs * /
    .clock(clock), 
    .clr(wire_reset_contador_vidas | reset), 
    .ld(1'b0), 
    .ent(1'b1), 
    .enp(wire_enable_decrementador), 
    .D(4'b0011), 
    /* outputs * /
    .Q(wire_quantidade_vidas), 
    .rco(wire_vidas)
);

    
wire [5:0] wire_saida_reg_jogada;

  registrador_n #(6) reg_jogada (
    /* inputs * /
    .clock  (clock),
    .clear  (wire_reset_reg_jogada),
    .enable (wire_enable_reg_jogada),
    .D      (chaves),
    /* output * /
    .Q      (wire_saida_reg_jogada)
);


wire jogada_up;
wire jogada_down;
wire jogada_right;
wire jogada_left;
wire jogada_especial;
wire jogada_tiro;

or (wire_ocorreu_jogada, jogada_up, jogada_down, jogada_right, jogada_left, jogada_especial, jogada_tiro);

mux_reg_jogada mux_jogada(
    .select_mux_jogada (wire_saida_reg_jogada[5:2]),
    /* output * /
    .saida_mux       (wire_opcode_mux_out)
);


contador_m #(1024, 10) contador_pontuacao (
    /* inputs * /
    .clock(clock),
    .zera_as(wire_reset_pontuacao_uc_principal),
    .zera_s(),
    .conta(wire_incrementa_pontos_uc_compara_tiros_e_asteroides),
    /* outputs * /
    .Q(db_pontos),
    .fim(),
    .meio()
  );


edge_detector edge_detector_jogada_up(
    .clock(clock),
    .reset(1'b0),
    .sinal(chaves[0]),
    .pulso(jogada_up)
);

edge_detector edge_detector_jogada_down(
    .clock(clock),
    .reset(1'b0),
    .sinal(chaves[1]),
    .pulso(jogada_down)
);

edge_detector edge_detector_jogada_right(
    .clock(clock),
    .reset(1'b0),
    .sinal(chaves[2]),
    .pulso(jogada_right)
);

edge_detector edge_detector_jogada_left(
    .clock(clock),
    .reset(1'b0),
    .sinal(chaves[3]),
    .pulso(jogada_left)
);

edge_detector edge_detector_jogada_especial(
    .clock(clock),
    .reset(1'b0),
    .sinal(chaves[4]),
    .pulso(jogada_especial)
);

edge_detector edge_detector_jogada_tiro(
    .clock(clock),
    .reset(1'b0),
    .sinal(chaves[5]),
    .pulso(jogada_tiro)
);

edge_detector edge_detector_tiro(
    .clock(clock),
    .reset(1'b0),
    .sinal(wire_saida_reg_jogada[0]),
    .pulso(wire_ocorreu_tiro)
);




endmodule


module asteroide(
    input clock,
    input conta_contador_aste,
    input reset_contador_aste,
    input [1:0] select_mux_pos_aste,
    input select_mux_coor_aste,
    input select_soma_sub_aste,
    input enable_reg_nave,
    input reset_reg_nave,
    input enable_mem_aste,
    input enable_load_aste,

    input new_load_aste,
    input new_destruido_aste,

    input reset_gerador_random,

    output colisao_aste_com_nave,
    output rco_contador_aste,
    output [1:0] opcode_aste,
    output destruido_aste,
    output loaded_aste,

    output [3:0] aste_coor_x,
    output [3:0] aste_coor_y,

    //saidas que podem ser retiradas
    output [3:0] db_contador_aste,
    output [4:0] db_wire_saida_som_sub_aste
);
         
    wire [3:0] wire_saida_contador;
    wire [3:0] wire_saida_mux_coor;
    wire [9:0] wire_saida_mux_pos;
    wire [9:0] wire_saida_memoria_aste;
    wire wire_select_som_sub;
    wire [4:0] wire_saida_som_sub;
    wire wire_saida_comparador_x;
    wire wire_saida_comparador_y;
    wire [9:0] wire_saida_reg_nave;
    wire [1:0] memoria_loaded;
    wire wire_rco_contador_aste;

    assign db_contador_aste = wire_saida_contador;
    assign db_wire_saida_som_sub_aste = wire_saida_som_sub;

    assign loaded_aste = memoria_loaded[1];
    assign destruido_aste = memoria_loaded[0];
    assign opcode_aste = wire_saida_memoria_aste[1:0];
    assign aste_coor_x = wire_saida_memoria_aste[9:6];
    assign aste_coor_y = wire_saida_memoria_aste[5:2];
    assign rco_contador_aste = wire_rco_contador_aste;
    assign wire_select_som_sub = select_soma_sub_aste;

contador_m #(16, 4) contador(
    /* inputs * /
    .clock   (clock),
    .zera_as (reset_contador_aste),
    .zera_s  (),
    .conta   (conta_contador_aste),
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*/
